# Fritzing sketch Circuit diagram (saved by Fritzing 0.9.3b)
breadboards: 1

parts:
  Part1 = Arduino Uno (Rev3)  # not connected
  Part2 = Arduino Ethernet Shield (Rev3)
  T1 = LM35 Temperature Sensor [package="TO92 [THT]"]
  LED1 = LED - 5mm [color="Red (633nm)" package="5 mm [THT]"]
  LCD1 = LCD screen
  R1 = Photocell (LDR) [package=THT]
  LED2 = LED - 5mm [color="Red (633nm)" package="5 mm [THT]"]
  R2 = Resistor [tolerance=±5% resistance=220 package=THT]
  R3 = Trimmer Potentiometer [maximum_resistance=10kΩ package=THT]

nets:
  N1: Part2.A0, R1.pin_1, R2.Pin_0
  N2: Part2.A1, T1.Vout
  N3: Part2.A4/SDA, LCD1.E
  N4: Part2.A5/SCL, LCD1.V0
  N5: Part2.D2, LCD1.DB7
  N6: Part2.PWM_D3, LCD1.DB6
  N7: Part2.SDCS, LCD1.DB5
  N8: Part2.PWM_D5, LCD1.DB4
  N9: Part2.PWM_D6, LED2.cathode
  N10: Part2.D7, LED1.cathode
  N11: Part2.3V3, T1.+Vs, R1.pin_0, R3.leg2
  5V: Part2.5V, LCD1.VDD
  GND: Part2.GND, T1.GND, LED1.anode, LCD1.VSS, LCD1.R/W, LED2.anode, R2.Pin_1, R3.leg1
  N12: LCD1.RS, R3.wiper

notes:
  Arduino Uno with Ethernet Shield
