# Fritzing sketch Circuit Diagram (saved by Fritzing 0.9.3b)
breadboards: 1

parts:
  Part1 = Arduino Uno (Rev3)
  LED1 = LED - 5mm [color="Red (633nm)" package="5 mm [THT]"]
  LED2 = LED - 5mm [color="Red (633nm)" package="5 mm [THT]"]
  R1 = Photocell (LDR) [package=THT]
  T1 = LM35 Temperature Sensor [package="TO92 [THT]"]
  T2 = LM35 Temperature Sensor [package="TO92 [THT]"]
  R2 = Resistor [tolerance=±5% resistance=100k package=THT]

nets:
  N1: Part1.A0, T1.Vout
  N2: Part1.A1, T2.Vout
  N3: Part1.A2, R1.pin_1, R2.Pin_0
  N4: Part1.3V3, LED1.anode, LED2.anode, R1.pin_0, T1.+Vs, T2.+Vs
  GND: Part1.GND, LED1.cathode, LED2.cathode, T1.GND, T2.GND, R2.Pin_1
