# Fritzing sketch currentBreadboardDiagram (saved by Fritzing 0.9.3b)
circuit board: 5.83065cm x 11.2504cm
breadboards: 1

parts:
  Arduino_Pro_Mini = Arduino Mini (Rev5)
  Raspberry_Pi_3 = Raspberry Pi 3 [part_number=RPI-3-V1.2]
  part = DS18B20 1-Wire Temperature Sensor [part_number=DS18B20]
  R5 = Resistor [tolerance=±5% resistance=4k package="1206 [SMD]"]
  R6 = Resistor [tolerance=±5% resistance=330 package="2010 [SMD]"]
  R7 = Resistor [tolerance=±5% resistance=330 package="1206 [SMD]"]
  LED1 = LEDs [package=led10mm]
  LED2 = LEDs [package=led10mm]

nets:
  GND: Arduino_Pro_Mini.GND, Raspberry_Pi_3.GND, part.GND, R6.Pin_1, R7.Pin_1
  VCC: Arduino_Pro_Mini.VCC, Raspberry_Pi_3.5V
  5V: Arduino_Pro_Mini.5V, part.VDD
  N1: Arduino_Pro_Mini.A0, part.DQ, R5.Pin_0
  N2: Arduino_Pro_Mini.TX, Raspberry_Pi_3.GIPO15
  N3: Arduino_Pro_Mini.RX, Raspberry_Pi_3.GIPO14
  N4: Raspberry_Pi_3.GIPO17, LED1.C
  N5: Raspberry_Pi_3.GIPO18, LED2.C
  N6: R6.Pin_0, LED1.A
  N7: R7.Pin_0, LED2.A

notes:
  Raspberry Pi has the camera module attached and is powered by the USB port
  4k ohm resistor between data and power
  DS18B20 is waterproof and on a long wire
  2 leds to simulate the output of the project one is for the heater the other is for the lighting system
  Arduino and Raspberry Pi are connected via 5v dc and ground. With Rx on the Raspberry Pi connected to Tx on the Arduino and Tx on the Raspberry Pi connected to Rx on the Arduino
